// Logisim project brainfuck.circ as structural Verilog: 1 circuit, main circuit main
module main (
);

  wire and_1_out, and_2_out, and_3_out, and_4_out, and_5_out, and_6_out, and_7_out, and_8_out, and_9_out,
       button_1_out, button_2_out, button_3_out, button_4_out, clock_1_out, comparator_1_eq,
       controlled_buffer_1_out, controlled_buffer_2_out, counter_1_q, decoder_1_out0, decoder_1_out1,
       decoder_1_out2, decoder_1_out3, decoder_1_out4, decoder_1_out5, decoder_1_out6, decoder_1_out7,
       not_1_out, not_2_out, not_3_out, not_4_out, not_5_out, not_6_out, not_7_out, not_8_out, not_9_out,
       or_1_out, or_2_out, or_3_out, or_4_out, or_5_out, or_6_out, or_7_out;
  wire [2:0] ram_1_data;
  wire [6:0] bitselector_2_out, keyboard_1_data;
  wire [7:0] adder_1_out, bit_extender_1_out, bitselector_1_out, bitselector_3_out, ram_3_data,
       subtractor_1_out;
  wire [15:0] counter_2_q, counter_4_q, counter_5_q, ram_2_data;

  Clock clock_1 (.out(clock_1_out));
  assign controlled_buffer_1_out = not_1_out ? clock_1_out : 1'bz;  // Controlled_Buffer controlled_buffer_1
  not not_1 (not_1_out, counter_1_q);
  and and_1 (and_1_out, clock_1_out, button_1_out, decoder_1_out5);
  and and_2 (and_2_out, controlled_buffer_2_out, not_2_out);
  not not_2 (not_2_out, controlled_buffer_1_out);
  Pull_Resistor pull_resistor_1 (.node(controlled_buffer_1_out));
  Counter #(.width(1), .max('h1)) counter_1 (
    .Q(counter_1_q), .clk(decoder_1_out5), .clr(or_1_out));  // open: load, D, count, carry
  or or_1 (or_1_out, and_1_out, button_2_out);
  Button button_1 (.out(button_1_out));
  Counter #(.width(16), .max('hffff)) counter_2 (
    .load(and_2_out), .D(ram_2_data), .count(not_3_out), .Q(counter_2_q), .clk(or_2_out), .clr(button_2_out));  // open: carry
  not not_3 (not_3_out, and_2_out);
  or or_2 (or_2_out, and_2_out, controlled_buffer_1_out);
  Button button_2 (.out(button_2_out));
  LED led_1 (.in(decoder_1_out5));
  Keyboard keyboard_1 (.clk(button_1_out), .clr(button_3_out), .data(keyboard_1_data));  // open: re, avail
  Button button_3 (.out(button_3_out));
  assign controlled_buffer_2_out = and_9_out ? decoder_1_out7 : 1'bz;  // Controlled_Buffer controlled_buffer_2
  Pull_Resistor pull_resistor_2 (.node(controlled_buffer_2_out));
  Button button_4 (.out(button_4_out));
  RAM #(.addrWidth(16), .dataWidth(3), .bus("separate")) ram_1 (
    .addr(counter_2_q), .data(ram_1_data), .clr(button_4_out));  // open: din, str, sel, clk, ld
  not not_4 (not_4_out, controlled_buffer_1_out);
  assign bit_extender_1_out = {{1{1'b0}}, keyboard_1_data};  // Bit_Extender bit_extender_1
  Counter #(.width(16), .max('hffff)) counter_3 (.clk(decoder_1_out4));  // open: load, D, count, Q, carry, clr
  Decoder #(.select(3)) decoder_1 (
    .out0(decoder_1_out0), .out1(decoder_1_out1), .out2(decoder_1_out2), .out3(decoder_1_out3),
    .out4(decoder_1_out4), .out5(decoder_1_out5), .out6(decoder_1_out6), .out7(decoder_1_out7),
    .sel(ram_1_data));  // open: en
  and and_3 (and_3_out, decoder_1_out5, button_1_out);
  and and_4 (and_4_out, decoder_1_out6, not_4_out);
  not not_5 (not_5_out, not_4_out);
  not not_6 (not_6_out, clock_1_out);
  not not_7 (not_7_out, decoder_1_out5);
  Counter #(.width(16), .max('hffff)) counter_4 (
    .load(decoder_1_out7), .count(or_3_out), .Q(counter_4_q), .clk(and_7_out), .clr(button_2_out));  // open: D, carry
  or or_3 (or_3_out, decoder_1_out7, decoder_1_out6);
  or or_4 (or_4_out, and_4_out, decoder_1_out7);
  and and_5 (and_5_out, not_6_out, decoder_1_out4);
  Counter #(.width(16), .max('hffff)) counter_5 (
    .load(decoder_1_out1), .count(or_5_out), .Q(counter_5_q), .clk(not_8_out), .clr(button_2_out));  // open: D, carry
  or or_5 (or_5_out, decoder_1_out1, decoder_1_out0);
  not not_8 (not_8_out, controlled_buffer_1_out);
  BitSelector #(.width(16), .group(8)) bitselector_1 (
    .in({bitselector_3_out, bit_extender_1_out}), .out(bitselector_1_out), .sel(not_7_out));
  and and_6 (and_6_out, ~and_9_out, not_5_out);  // AND_Gate
  or or_6 (or_6_out, decoder_1_out2, decoder_1_out3);
  and and_7 (and_7_out, ~and_6_out, or_4_out);  // AND_Gate
  or or_7 (or_7_out, and_8_out, and_3_out);
  and and_8 (and_8_out, or_6_out, ~controlled_buffer_1_out);  // AND_Gate
  RAM #(.addrWidth(16), .dataWidth(16), .bus("separate")) ram_2 (
    .addr(counter_4_q), .din(counter_2_q), .data(ram_2_data), .str(and_4_out), .clk(and_7_out),
    .clr(button_2_out));  // open: sel, ld
  RAM #(.addrWidth(16), .bus("separate")) ram_3 (
    .addr(counter_5_q), .din(bitselector_1_out), .data(ram_3_data), .str(or_7_out), .clk(or_7_out),
    .clr(button_2_out));  // open: sel, ld
  Comparator comparator_1 (.a(ram_3_data), .b({8{1'b0}}), .eq(comparator_1_eq));  // open: gt, lt
  and and_9 (and_9_out, decoder_1_out7, not_9_out);
  BitSelector #(.group(7)) bitselector_2 (.in(ram_3_data), .out(bitselector_2_out), .sel(1'b0));
  Adder adder_1 (.a(ram_3_data), .b(8'h1), .out(adder_1_out));  // open: cin, cout
  Subtractor subtractor_1 (.a(ram_3_data), .b(8'h1), .out(subtractor_1_out));  // open: bin, bout
  not not_9 (not_9_out, comparator_1_eq);
  TTY tty_1 (.data(bitselector_2_out), .clk(and_5_out), .clr(button_2_out));  // open: we
  BitSelector #(.width(16), .group(8)) bitselector_3 (
    .in({subtractor_1_out, adder_1_out}), .out(bitselector_3_out), .sel(decoder_1_out3));

  // Notes on the sheet:
  //   Записать
  //   Сброс состояния
  //   0 - >
  //   1 - <
  //   2 - +
  //   3 - -
  //   Ожидание ввода 
  //   4 - .
  //   5 - ,
  //   6 - [
  //   7 - ]
  //   Сброс программы
endmodule
